# Fritzing sketch Dr-Robot (saved by Fritzing 0.9.1b)
breadboards: 1

parts:
  R1 = Resistor [tolerance=±5% resistance=220 package=THT]
  LED1 = LED - 5mm [color="Red (633nm)" package="5 mm [THT]"]
  J1 = Piezo Speaker
  Raspberry_Pi1 = Raspberry Pi B+
  R2 = Resistor [tolerance=±5% resistance=220 package=THT]
  LED2 = LED - 5mm [color="Red (633nm)" package="5 mm [THT]"]
  LED3 = LED - 5mm [color="Red (633nm)" package="5 mm [THT]"]
  R4 = Resistor [tolerance=±5% resistance=220 package=THT]

nets:
  N1: R1.Pin_0, J1.pin1, Raspberry_Pi1.GND, R2.Pin_0, R4.Pin_0
  N2: R1.Pin_1, LED2.cathode
  N3: LED1.cathode, R4.Pin_1
  N4: LED1.anode, Raspberry_Pi1.GPIO22
  N5: J1.pin2, Raspberry_Pi1.GPIO10
  N6: Raspberry_Pi1.GPIO17, LED3.anode
  N7: Raspberry_Pi1.GPIO27, LED2.anode
  N8: R2.Pin_1, LED3.cathode

notes:
  Connects to surgery tool (Tweezers)
